// Logisim project ece422L_lab7_full_adder.circ as structural Verilog: 2 circuits, main circuit main
module main (
  input  A1,
  input  B,
  input  Cin,
  output SUM,
  output CARRY_OUT
);

  wire and_1_out, and_2_out, xor_1_out;

  xor xor_1 (xor_1_out, A1, B);
  and and_1 (and_1_out, A1, B);
  xor xor_2 (SUM, xor_1_out, Cin);
  and and_2 (and_2_out, xor_1_out, Cin);
  or or_1 (CARRY_OUT, and_2_out, and_1_out);
endmodule

module One_Bit_ALU (
  input  CIN,
  input  A,
  input  A_INVERT,
  input  B,
  input  B_INVERT,
  input  LESS,
  input  [1:0] ALU_CONTROL,
  output ALU_RESULT,
  output COUT
);

  wire adder_1_out, and_1_out, multiplexer_1_out, multiplexer_2_out, not_1_out, not_2_out, or_1_out;

  not not_1 (not_1_out, A);
  not not_2 (not_2_out, B);
  Multiplexer multiplexer_1 (.in0(A), .in1(not_1_out), .out(multiplexer_1_out), .sel(A_INVERT));
  Multiplexer multiplexer_2 (.in0(B), .in1(not_2_out), .out(multiplexer_2_out), .sel(B_INVERT));
  and and_1 (and_1_out, multiplexer_1_out, multiplexer_2_out);
  or or_1 (or_1_out, multiplexer_1_out, multiplexer_2_out);
  Adder #(.width(1)) adder_1 (.a(multiplexer_1_out), .b(multiplexer_2_out), .out(adder_1_out), .cin(CIN), .cout(COUT));
  Multiplexer #(.select(2)) multiplexer_3 (
    .in0(and_1_out), .in1(or_1_out), .in2(adder_1_out), .in3(LESS), .out(ALU_RESULT), .sel(ALU_CONTROL));
endmodule
