// Logisim project ece422L_lab7_mux.circ as structural Verilog: 1 circuit, main circuit main
module main (
  input  SEL,
  input  IN1,
  input  IN2,
  input  A1,
  input  B,
  input  Cin,
  output OUT1,
  output SUM,
  output CARRY_OUT
);

  wire and_1_out, and_2_out, and_3_out, and_4_out, not_1_out, xor_1_out;

  not not_1 (not_1_out, SEL);
  xor xor_1 (xor_1_out, A1, B);
  and and_1 (and_1_out, A1, B);
  and and_2 (and_2_out, not_1_out, IN1);
  and and_3 (and_3_out, SEL, IN2);
  or or_1 (OUT1, and_2_out, and_3_out);
  xor xor_2 (SUM, xor_1_out, Cin);
  and and_4 (and_4_out, xor_1_out, Cin);
  or or_2 (CARRY_OUT, and_4_out, and_1_out);

  // Notes on the sheet:
  //   ECE 422L
  //   March 28, 2025
  //   Olayinka Olowookere
  //   Lab7: Introduction
endmodule
