// Logisim project Lab_10.circ as structural Verilog: 3 circuits, main circuit Program_Counter
module Program_Counter (
  input  [31:0] DIN,
  input  CLK,
  output [31:0] DOUT
);

  PC_Register_32_Bit pc_register_32_bit_1 (.DIN(DIN), .ENABLE(1'b1), .CLK(CLK), .RST(1'b0), .DOUT(DOUT));

  // Notes on the sheet:
  //   Olayinka Olowookere
  //   ECE 422L
  //   Lab 10: Program Counter
endmodule

module Control_Unit (
  input  [5:0] OPCODE,
  output RegDst,
  output ALUSrc,
  output MemtoReg,
  output RegWrite,
  output MemRead,
  output MemWrite,
  output Branch,
  output ALUOp1,
  output ALUOp0,
  output Jump
);

  and and_1 (ALUOp1, ~OPCODE[5], ~OPCODE[4], ~OPCODE[3], ~OPCODE[2], ~OPCODE[1], ~OPCODE[0]);  // AND_Gate
  and and_2 (MemRead, OPCODE[5], ~OPCODE[4], ~OPCODE[3], ~OPCODE[2], OPCODE[1], OPCODE[0]);  // AND_Gate
  and and_3 (MemWrite, OPCODE[5], ~OPCODE[4], OPCODE[3], ~OPCODE[2], OPCODE[1], OPCODE[0]);  // AND_Gate
  and and_4 (ALUOp0, ~OPCODE[5], ~OPCODE[4], ~OPCODE[3], OPCODE[2], ~OPCODE[1], ~OPCODE[0]);  // AND_Gate
  and and_5 (Jump, ~OPCODE[5], ~OPCODE[4], ~OPCODE[3], ~OPCODE[2], OPCODE[1], ~OPCODE[0]);  // AND_Gate
  or or_1 (ALUSrc, MemRead, MemWrite);
  or or_2 (RegWrite, ALUOp1, MemRead);

  assign Branch = ALUOp0;
  assign MemtoReg = MemRead;
  assign RegDst = ALUOp1;
endmodule

module ALU_Control_Unit (
  input  [1:0] ALUOp,
  input  [5:0] Funct,
  input  [3:0] ALUControl
);

  wire and_1_out, comparator_1_gt, comparator_2_gt;

  Comparator #(.mode("unsigned"), .width(2)) comparator_1 (.a(ALUOp), .b(2'b10), .gt(comparator_1_gt));  // open: eq, lt
  Comparator #(.mode("unsigned"), .width(6)) comparator_2 (
    .a(Funct), .b(6'b100000), .gt(comparator_2_gt));  // open: eq, lt
  and and_1 (and_1_out, comparator_1_gt, comparator_2_gt);
  Multiplexer #(.width(4)) multiplexer_1 (.in1(4'b0010), .out(ALUControl), .sel(and_1_out));  // open: in0
endmodule
