// Logisim project ece422L_lab8_one_bit_alu.circ as structural Verilog: 4 circuits, main circuit Equality_Check_ALU
module main (
  input  A1,
  input  B,
  input  Cin,
  output SUM,
  output CARRY_OUT
);

  wire and_1_out, and_2_out, xor_1_out;

  xor xor_1 (xor_1_out, A1, B);
  and and_1 (and_1_out, A1, B);
  xor xor_2 (SUM, xor_1_out, Cin);
  and and_2 (and_2_out, xor_1_out, Cin);
  or or_1 (CARRY_OUT, and_2_out, and_1_out);
endmodule

module One_Bit_ALU (
  input  CIN,
  input  A,
  input  B,
  input  LESS,
  input  [3:0] ALU_CONTROL,
  output ALU_RESULT,
  output C_OUT,
  output SET
);

  wire and_1_out, multiplexer_1_out, multiplexer_2_out, not_1_out, not_2_out, or_1_out;

  not not_1 (not_1_out, A);
  not not_2 (not_2_out, B);
  Multiplexer multiplexer_1 (.in0(A), .in1(not_1_out), .out(multiplexer_1_out), .sel(ALU_CONTROL[3]));
  Multiplexer multiplexer_2 (.in0(B), .in1(not_2_out), .out(multiplexer_2_out), .sel(ALU_CONTROL[2]));
  and and_1 (and_1_out, multiplexer_1_out, multiplexer_2_out);
  or or_1 (or_1_out, multiplexer_1_out, multiplexer_2_out);
  Adder #(.width(1)) adder_1 (.a(multiplexer_1_out), .b(multiplexer_2_out), .out(SET), .cin(CIN), .cout(C_OUT));
  Multiplexer #(.select(2)) multiplexer_3 (
    .in0(and_1_out), .in1(or_1_out), .in2(SET), .in3(LESS), .out(ALU_RESULT), .sel(ALU_CONTROL[1:0]));

  // Notes on the sheet:
  //   Olayinka Olowookere
  //   ECE 422L
  //   Lab 8 - ALU DESIGN
endmodule

module Four_Bit_ALU (
  input  A0,
  input  B0,
  input  [3:0] ALU_CONTROL,
  input  A1,
  input  B1,
  input  A2,
  input  B2,
  input  A3,
  input  B3,
  output R0,
  output R1,
  output R2,
  output R3,
  output C_OUT
);

  wire one_bit_alu_1_c_out, one_bit_alu_2_c_out, one_bit_alu_3_c_out, one_bit_alu_4_set, undriven, undriven_2;

  One_Bit_ALU one_bit_alu_1 (
    .CIN(ALU_CONTROL[2]), .A(A0), .B(B0), .LESS(one_bit_alu_4_set), .ALU_CONTROL(ALU_CONTROL),
    .ALU_RESULT(R0), .C_OUT(one_bit_alu_1_c_out));  // open: SET
  One_Bit_ALU one_bit_alu_2 (
    .CIN(one_bit_alu_1_c_out), .A(A1), .B(B1), .LESS(1'b0), .ALU_CONTROL(ALU_CONTROL), .ALU_RESULT(R1),
    .C_OUT(one_bit_alu_2_c_out));  // open: SET
  One_Bit_ALU one_bit_alu_3 (
    .CIN(one_bit_alu_2_c_out), .A(A2), .B(B2), .LESS(undriven), .ALU_CONTROL(ALU_CONTROL), .ALU_RESULT(R2),
    .C_OUT(one_bit_alu_3_c_out));  // open: SET
  One_Bit_ALU one_bit_alu_4 (
    .CIN(one_bit_alu_3_c_out), .A(A3), .B(B3), .LESS(undriven_2), .ALU_CONTROL(ALU_CONTROL), .ALU_RESULT(R3),
    .C_OUT(C_OUT), .SET(one_bit_alu_4_set));
endmodule

module Equality_Check_ALU (
  input  [3:0] ALU_CONTROL,
  input  A27,
  input  B27,
  input  A28,
  input  B28,
  input  A29,
  input  B29,
  input  A30,
  input  B30,
  input  A31,
  input  B31,
  input  [31:0] A,
  input  [31:0] B,
  input  [31:0] in_14,
  output Z,
  output Overflow,
  output C,
  output [31:0] R_OUT
);

  wire C_IN, C_OUT, comparator_1_eq, comparator_2_eq, one_bit_alu_1_c_out, one_bit_alu_2_c_out,
       one_bit_alu_3_c_out, one_bit_alu_4_c_out, one_bit_alu_5_c_out, one_bit_alu_6_c_out,
       one_bit_alu_7_c_out, one_bit_alu_8_c_out, one_bit_alu_9_c_out, one_bit_alu_10_c_out,
       one_bit_alu_11_c_out, one_bit_alu_12_c_out, one_bit_alu_13_c_out, one_bit_alu_15_c_out,
       one_bit_alu_16_c_out, one_bit_alu_17_c_out, one_bit_alu_18_c_out, one_bit_alu_19_c_out,
       one_bit_alu_20_c_out, one_bit_alu_21_c_out, one_bit_alu_22_c_out, one_bit_alu_23_c_out,
       one_bit_alu_24_c_out, one_bit_alu_25_c_out, one_bit_alu_26_c_out, one_bit_alu_27_c_out,
       one_bit_alu_28_c_out, one_bit_alu_29_c_out, one_bit_alu_30_c_out, one_bit_alu_31_c_out;

  Comparator #(.width(4)) comparator_1 (.a(4'b0010), .b(ALU_CONTROL), .eq(comparator_1_eq));  // open: gt, lt
  Comparator #(.width(4)) comparator_2 (.a(ALU_CONTROL), .b(4'b0110), .eq(comparator_2_eq));  // open: gt, lt
  xor xor_1 (Overflow, C_OUT, C_IN);
  or or_1 (C, comparator_1_eq, comparator_2_eq);
  One_Bit_ALU one_bit_alu_1 (
    .CIN(ALU_CONTROL[2]), .A(A[0]), .B(B[0]), .LESS(C_OUT), .ALU_CONTROL(ALU_CONTROL), .ALU_RESULT(R_OUT[0]),
    .C_OUT(one_bit_alu_1_c_out));  // open: SET
  One_Bit_ALU one_bit_alu_2 (
    .CIN(one_bit_alu_1_c_out), .A(A[1]), .B(B[1]), .LESS(1'b0), .ALU_CONTROL(ALU_CONTROL),
    .ALU_RESULT(R_OUT[1]), .C_OUT(one_bit_alu_2_c_out));  // open: SET
  One_Bit_ALU one_bit_alu_3 (
    .CIN(one_bit_alu_2_c_out), .A(A[2]), .B(B[2]), .LESS(1'b0), .ALU_CONTROL(ALU_CONTROL),
    .ALU_RESULT(R_OUT[2]), .C_OUT(one_bit_alu_3_c_out));  // open: SET
  One_Bit_ALU one_bit_alu_4 (
    .CIN(one_bit_alu_3_c_out), .A(A[3]), .B(B[3]), .LESS(1'b0), .ALU_CONTROL(ALU_CONTROL),
    .ALU_RESULT(R_OUT[3]), .C_OUT(one_bit_alu_4_c_out));  // open: SET
  One_Bit_ALU one_bit_alu_5 (
    .CIN(one_bit_alu_4_c_out), .A(A[4]), .B(B[4]), .LESS(1'b0), .ALU_CONTROL(ALU_CONTROL),
    .ALU_RESULT(R_OUT[4]), .C_OUT(one_bit_alu_5_c_out));  // open: SET
  One_Bit_ALU one_bit_alu_6 (
    .CIN(one_bit_alu_5_c_out), .A(A[5]), .B(B[5]), .LESS(1'b0), .ALU_CONTROL(ALU_CONTROL),
    .ALU_RESULT(R_OUT[5]), .C_OUT(one_bit_alu_6_c_out));  // open: SET
  One_Bit_ALU one_bit_alu_7 (
    .CIN(one_bit_alu_6_c_out), .A(A[7]), .B(B[7]), .LESS(1'b0), .ALU_CONTROL(ALU_CONTROL),
    .ALU_RESULT(R_OUT[6]), .C_OUT(one_bit_alu_7_c_out));  // open: SET
  One_Bit_ALU one_bit_alu_8 (
    .CIN(one_bit_alu_7_c_out), .A(A[8]), .B(B[8]), .LESS(1'b0), .ALU_CONTROL(ALU_CONTROL),
    .ALU_RESULT(R_OUT[7]), .C_OUT(one_bit_alu_8_c_out));  // open: SET
  One_Bit_ALU one_bit_alu_9 (
    .CIN(one_bit_alu_8_c_out), .A(A[8]), .B(B[8]), .LESS(1'b0), .ALU_CONTROL(ALU_CONTROL),
    .ALU_RESULT(R_OUT[8]), .C_OUT(one_bit_alu_9_c_out));  // open: SET
  One_Bit_ALU one_bit_alu_10 (
    .CIN(one_bit_alu_9_c_out), .A(A[9]), .B(B[9]), .LESS(1'b0), .ALU_CONTROL(ALU_CONTROL),
    .ALU_RESULT(R_OUT[9]), .C_OUT(one_bit_alu_10_c_out));  // open: SET
  One_Bit_ALU one_bit_alu_11 (
    .CIN(one_bit_alu_10_c_out), .A(A[10]), .B(B[10]), .LESS(1'b0), .ALU_CONTROL(ALU_CONTROL),
    .ALU_RESULT(R_OUT[10]), .C_OUT(one_bit_alu_11_c_out));  // open: SET
  One_Bit_ALU one_bit_alu_12 (
    .CIN(one_bit_alu_15_c_out), .A(A[12]), .B(B[12]), .LESS(1'b0), .ALU_CONTROL(ALU_CONTROL),
    .ALU_RESULT(R_OUT[12]), .C_OUT(one_bit_alu_12_c_out));  // open: SET
  One_Bit_ALU one_bit_alu_13 (
    .CIN(one_bit_alu_12_c_out), .A(A[13]), .B(B[13]), .LESS(1'b0), .ALU_CONTROL(ALU_CONTROL),
    .ALU_RESULT(R_OUT[13]), .C_OUT(one_bit_alu_13_c_out));  // open: SET
  One_Bit_ALU one_bit_alu_14 (
    .CIN(one_bit_alu_13_c_out), .A(A[14]), .B(B[14]), .LESS(1'b0), .ALU_CONTROL(ALU_CONTROL),
    .ALU_RESULT(R_OUT[14]), .C_OUT(C_IN));  // open: SET
  One_Bit_ALU one_bit_alu_15 (
    .CIN(one_bit_alu_11_c_out), .A(A[11]), .B(B[11]), .LESS(1'b0), .ALU_CONTROL(ALU_CONTROL),
    .ALU_RESULT(R_OUT[11]), .C_OUT(one_bit_alu_15_c_out));  // open: SET
  One_Bit_ALU one_bit_alu_16 (
    .CIN(C_IN), .A(A[15]), .B(B[15]), .LESS(1'b0), .ALU_CONTROL(ALU_CONTROL), .ALU_RESULT(R_OUT[15]),
    .C_OUT(one_bit_alu_16_c_out));  // open: SET
  One_Bit_ALU one_bit_alu_17 (
    .CIN(one_bit_alu_16_c_out), .A(A[16]), .B(B[16]), .LESS(1'b0), .ALU_CONTROL(ALU_CONTROL),
    .ALU_RESULT(R_OUT[16]), .C_OUT(one_bit_alu_17_c_out));  // open: SET
  One_Bit_ALU one_bit_alu_18 (
    .CIN(one_bit_alu_17_c_out), .A(A[17]), .B(B[17]), .LESS(1'b0), .ALU_CONTROL(ALU_CONTROL),
    .ALU_RESULT(R_OUT[17]), .C_OUT(one_bit_alu_18_c_out));  // open: SET
  One_Bit_ALU one_bit_alu_19 (
    .CIN(one_bit_alu_18_c_out), .A(A[18]), .B(B[18]), .LESS(1'b0), .ALU_CONTROL(ALU_CONTROL),
    .ALU_RESULT(R_OUT[18]), .C_OUT(one_bit_alu_19_c_out));  // open: SET
  One_Bit_ALU one_bit_alu_20 (
    .CIN(one_bit_alu_23_c_out), .A(A[20]), .B(B[20]), .LESS(1'b0), .ALU_CONTROL(ALU_CONTROL),
    .ALU_RESULT(R_OUT[20]), .C_OUT(one_bit_alu_20_c_out));  // open: SET
  One_Bit_ALU one_bit_alu_21 (
    .CIN(one_bit_alu_20_c_out), .A(A[21]), .B(A[21]), .LESS(1'b0), .ALU_CONTROL(ALU_CONTROL),
    .ALU_RESULT(R_OUT[21]), .C_OUT(one_bit_alu_21_c_out));  // open: SET
  One_Bit_ALU one_bit_alu_22 (
    .CIN(one_bit_alu_21_c_out), .A(A[8]), .B(A[8]), .LESS(1'b0), .ALU_CONTROL(ALU_CONTROL),
    .ALU_RESULT(R_OUT[22]), .C_OUT(one_bit_alu_22_c_out));  // open: SET
  One_Bit_ALU one_bit_alu_23 (
    .CIN(one_bit_alu_19_c_out), .A(A[19]), .B(B[19]), .LESS(1'b0), .ALU_CONTROL(ALU_CONTROL),
    .ALU_RESULT(R_OUT[19]), .C_OUT(one_bit_alu_23_c_out));  // open: SET
  One_Bit_ALU one_bit_alu_24 (
    .CIN(one_bit_alu_22_c_out), .A(A[23]), .B(A[23]), .LESS(1'b0), .ALU_CONTROL(ALU_CONTROL),
    .ALU_RESULT(R_OUT[23]), .C_OUT(one_bit_alu_24_c_out));  // open: SET
  One_Bit_ALU one_bit_alu_25 (
    .CIN(one_bit_alu_24_c_out), .A(A[24]), .B(B[24]), .LESS(1'b0), .ALU_CONTROL(ALU_CONTROL),
    .ALU_RESULT(R_OUT[24]), .C_OUT(one_bit_alu_25_c_out));  // open: SET
  One_Bit_ALU one_bit_alu_26 (
    .CIN(one_bit_alu_25_c_out), .A(A[25]), .B(A[16]), .LESS(1'b0), .ALU_CONTROL(ALU_CONTROL),
    .ALU_RESULT(R_OUT[25]), .C_OUT(one_bit_alu_26_c_out));  // open: SET
  One_Bit_ALU one_bit_alu_27 (
    .CIN(one_bit_alu_26_c_out), .A(A[16]), .B(A[16]), .LESS(1'b0), .ALU_CONTROL(ALU_CONTROL),
    .ALU_RESULT(R_OUT[26]), .C_OUT(one_bit_alu_27_c_out));  // open: SET
  One_Bit_ALU one_bit_alu_28 (
    .CIN(one_bit_alu_27_c_out), .A(A27), .B(B27), .LESS(1'b0), .ALU_CONTROL(ALU_CONTROL),
    .ALU_RESULT(R_OUT[27]), .C_OUT(one_bit_alu_28_c_out));  // open: SET
  One_Bit_ALU one_bit_alu_29 (
    .CIN(one_bit_alu_28_c_out), .A(A28), .B(B28), .LESS(1'b0), .ALU_CONTROL(ALU_CONTROL),
    .ALU_RESULT(R_OUT[28]), .C_OUT(one_bit_alu_29_c_out));  // open: SET
  One_Bit_ALU one_bit_alu_30 (
    .CIN(one_bit_alu_29_c_out), .A(A29), .B(B29), .LESS(1'b0), .ALU_CONTROL(ALU_CONTROL),
    .ALU_RESULT(R_OUT[29]), .C_OUT(one_bit_alu_30_c_out));  // open: SET
  One_Bit_ALU one_bit_alu_31 (
    .CIN(one_bit_alu_30_c_out), .A(A30), .B(B30), .LESS(1'b0), .ALU_CONTROL(ALU_CONTROL),
    .ALU_RESULT(R_OUT[30]), .C_OUT(one_bit_alu_31_c_out));  // open: SET
  One_Bit_ALU one_bit_alu_32 (
    .CIN(one_bit_alu_31_c_out), .A(A31), .B(B31), .LESS(1'b0), .ALU_CONTROL(ALU_CONTROL),
    .ALU_RESULT(R_OUT[31]), .C_OUT(C_OUT));  // open: SET
  nor nor_1 (Z, R_OUT[0], R_OUT[1], R_OUT[2], R_OUT[3], R_OUT[4], R_OUT[5], R_OUT[6], R_OUT[7], R_OUT[8], R_OUT[9], R_OUT[10], R_OUT[11], R_OUT[12], R_OUT[13], R_OUT[14], R_OUT[15], R_OUT[16], R_OUT[17], R_OUT[18], R_OUT[19], R_OUT[20], R_OUT[21], R_OUT[22], R_OUT[23], R_OUT[24], R_OUT[25], R_OUT[26], R_OUT[27], R_OUT[28], R_OUT[29], R_OUT[30], R_OUT[31]);

  // Other names for the same wires on the sheet: A27_t = A[27]; A28_t = A[28]; A29_t = A[29]; A30_t = A[30];
  //   A31_t = A[31]; B27_t = B[27]; B28_t = B[28]; B29_t = B[29]; B30_t = B[30]; B31_t = B[31]; R0 = R_OUT[0];
  //   R1 = R_OUT[1]; R2 = R_OUT[2]; R3 = R_OUT[3]; R4 = R_OUT[4]; R5 = R_OUT[5]; R6 = R_OUT[6]; R7 = R_OUT[7];
  //   R8 = R_OUT[8]; R9 = R_OUT[9]; R10 = R_OUT[10]; R11 = R_OUT[11]; R12 = R_OUT[12]; R13 = R_OUT[13];
  //   R14 = R_OUT[14]; R15 = R_OUT[15]; R16 = R_OUT[16]; R17 = R_OUT[17]; R18 = R_OUT[18]; R19 = R_OUT[19];
  //   R20 = R_OUT[20]; R21 = R_OUT[21]; R22 = R_OUT[22]; R23 = R_OUT[23]; R24 = R_OUT[24]; R25 = R_OUT[25];
  //   R26 = R_OUT[26]; R27 = R_OUT[27]; R28 = R_OUT[28]; R29 = R_OUT[29]; R30 = R_OUT[30]; R31 = R_OUT[31]
endmodule
