// Logisim project ece422L_register_32_bit.circ as structural Verilog: 3 circuits, main circuit PC_Register_4_Bit
module PC_Register_4_Bit (
  input  [3:0] DIN,
  input  ENABLE,
  input  CLK,
  input  RST,
  output [3:0] DOUT
);

  wire multiplexer_1_out, multiplexer_2_out, multiplexer_3_out, multiplexer_4_out;

  D_Flip_Flop d_ff_1 (.D(multiplexer_1_out), .clk(CLK), .Q(DOUT[3]), .reset(RST));  // open: Qn, preset
  Multiplexer multiplexer_1 (.in0(DOUT[3]), .in1(DIN[3]), .out(multiplexer_1_out), .sel(ENABLE));
  D_Flip_Flop d_ff_2 (.D(multiplexer_2_out), .clk(CLK), .Q(DOUT[2]), .reset(RST));  // open: Qn, preset
  Multiplexer multiplexer_2 (.in0(DOUT[2]), .in1(DIN[2]), .out(multiplexer_2_out), .sel(ENABLE));
  D_Flip_Flop d_ff_3 (.D(multiplexer_3_out), .clk(CLK), .Q(DOUT[1]), .reset(RST));  // open: Qn, preset
  Multiplexer multiplexer_3 (.in0(DOUT[1]), .in1(DIN[1]), .out(multiplexer_3_out), .sel(ENABLE));
  D_Flip_Flop d_ff_4 (.D(multiplexer_4_out), .clk(CLK), .Q(DOUT[0]), .reset(RST));  // open: Qn, preset
  Multiplexer multiplexer_4 (.in0(DOUT[0]), .in1(DIN[0]), .out(multiplexer_4_out), .sel(ENABLE));

  // Other names for the same wires on the sheet: C = CLK; D0 = DIN[0]; D1 = DIN[1]; D2 = DIN[2]; D3 = DIN[3];
  //   Q0 = DOUT[0]; Q1 = DOUT[1]; Q2 = DOUT[2]; Q3 = DOUT[3]; EN = ENABLE; R = RST

  // Notes on the sheet:
  //   Olayinka Olowookere
  //   ECE 422L
  //   Lab 9: Register File
endmodule

module PC_Register_32_Bit (
  input  [31:0] DIN,
  input  ENABLE,
  input  CLK,
  input  RST,
  output [31:0] DOUT
);

  PC_Register_4_Bit pc_register_4_bit_1 (.DIN(DIN[3:0]), .ENABLE(ENABLE), .CLK(CLK), .RST(RST), .DOUT(DOUT[3:0]));
  PC_Register_4_Bit pc_register_4_bit_2 (.DIN(DIN[7:4]), .ENABLE(ENABLE), .CLK(CLK), .RST(RST), .DOUT(DOUT[7:4]));
  PC_Register_4_Bit pc_register_4_bit_3 (.DIN(DIN[11:8]), .ENABLE(ENABLE), .CLK(CLK), .RST(RST), .DOUT(DOUT[11:8]));
  PC_Register_4_Bit pc_register_4_bit_4 (.DIN(DIN[15:12]), .ENABLE(ENABLE), .CLK(CLK), .RST(RST), .DOUT(DOUT[15:12]));
  PC_Register_4_Bit pc_register_4_bit_5 (.DIN(DIN[19:16]), .ENABLE(ENABLE), .CLK(CLK), .RST(RST), .DOUT(DOUT[19:16]));
  PC_Register_4_Bit pc_register_4_bit_6 (.DIN(DIN[23:20]), .ENABLE(ENABLE), .CLK(CLK), .RST(RST), .DOUT(DOUT[23:20]));
  PC_Register_4_Bit pc_register_4_bit_7 (.DIN(DIN[27:24]), .ENABLE(ENABLE), .CLK(CLK), .RST(RST), .DOUT(DOUT[27:24]));
  PC_Register_4_Bit pc_register_4_bit_8 (.DIN(DIN[31:28]), .ENABLE(ENABLE), .CLK(CLK), .RST(RST), .DOUT(DOUT[31:28]));

  // Other names for the same wires on the sheet: C = CLK; D3_D0[3:0] = DIN[3:0]; D7_D4[3:0] = DIN[7:4];
  //   D11_D8[3:0] = DIN[11:8]; D15_D12[3:0] = DIN[15:12]; D19_D16[3:0] = DIN[19:16]; D23_D20[3:0] = DIN[23:20];
  //   D27_D24[3:0] = DIN[27:24]; D31_D28[3:0] = DIN[31:28]; Q3_Q0[3:0] = DOUT[3:0]; Q7_Q4[3:0] = DOUT[7:4];
  //   Q11_Q8[3:0] = DOUT[11:8]; Q15_Q12[3:0] = DOUT[15:12]; Q19_Q16[3:0] = DOUT[19:16]; Q23_Q20[3:0] = DOUT[23:20];
  //   Q27_Q24[3:0] = DOUT[27:24]; Q31_Q28[3:0] = DOUT[31:28]; EN = ENABLE; R = RST

  // Notes on the sheet:
  //   Olayinka Olowookere
  //   ECE 422L
  //   Lab 9: Register File
endmodule

module Register_32_File (
  input  [31:0] Write_Data,
  input  Reg_Write,
  input  CLK,
  input  RST,
  input  [4:0] Select_DEC1,
  input  [4:0] MUX2,
  input  [4:0] MUX1,
  output [31:0] Read_Data2,
  output [31:0] Read_Data1
);

  wire EN0, EN1, EN2, EN3, EN4, EN5, EN6, EN7, EN8, EN9, EN10, EN11, EN12, EN13, EN14, EN15, EN16, EN17,
       EN18, EN19, EN20, EN21, EN22, EN23, EN24, EN25, EN26, EN27, EN28, EN29, EN30, EN31;
  wire [31:0] DOUT0, DOUT1, DOUT2, DOUT3, DOUT4, DOUT5, DOUT6, DOUT7, DOUT8, DOUT9, DOUT10, DOUT11, DOUT12,
       DOUT13, DOUT14, DOUT15, DOUT16, DOUT17, DOUT18, DOUT19, DOUT20, DOUT21, DOUT22, DOUT23, DOUT24,
       DOUT25, DOUT26, DOUT27, DOUT28, DOUT29, DOUT30, DOUT31;

  PC_Register_32_Bit R0 (.DIN(Write_Data), .ENABLE(EN0), .CLK(CLK), .RST(RST), .DOUT(DOUT0));
  PC_Register_32_Bit R1 (.DIN(Write_Data), .ENABLE(EN1), .CLK(CLK), .RST(RST), .DOUT(DOUT1));
  PC_Register_32_Bit R2 (.DIN(Write_Data), .ENABLE(EN2), .CLK(CLK), .RST(RST), .DOUT(DOUT2));
  PC_Register_32_Bit R3 (.DIN(Write_Data), .ENABLE(EN3), .CLK(CLK), .RST(RST), .DOUT(DOUT3));
  PC_Register_32_Bit R4 (.DIN(Write_Data), .ENABLE(EN4), .CLK(CLK), .RST(RST), .DOUT(DOUT4));
  PC_Register_32_Bit R5 (.DIN(Write_Data), .ENABLE(EN5), .CLK(CLK), .RST(RST), .DOUT(DOUT5));
  PC_Register_32_Bit R6 (.DIN(Write_Data), .ENABLE(EN6), .CLK(CLK), .RST(RST), .DOUT(DOUT6));
  PC_Register_32_Bit R7 (.DIN(Write_Data), .ENABLE(EN7), .CLK(CLK), .RST(RST), .DOUT(DOUT7));
  Multiplexer #(.select(5), .width(32)) multiplexer_1 (
    .in0(DOUT0), .in1(DOUT1), .in2(DOUT2), .in3(DOUT3), .in4(DOUT4), .in5(DOUT5), .in6(DOUT6), .in7(DOUT7),
    .in8(DOUT8), .in9(DOUT9), .in10(DOUT10), .in11(DOUT11), .in12(DOUT12), .in13(DOUT13), .in14(DOUT14),
    .in15(DOUT15), .in16(DOUT16), .in17(DOUT17), .in18(DOUT18), .in19(DOUT19), .in20(DOUT20), .in21(DOUT21),
    .in22(DOUT22), .in23(DOUT23), .in24(DOUT24), .in25(DOUT25), .in26(DOUT26), .in27(DOUT27), .in28(DOUT28),
    .in29(DOUT29), .in30(DOUT30), .in31(DOUT31), .out(Read_Data1), .sel(MUX1));
  PC_Register_32_Bit R8 (.DIN(Write_Data), .ENABLE(Reg_Write), .CLK(CLK), .RST(RST), .DOUT(DOUT8));
  PC_Register_32_Bit R9 (.DIN(Write_Data), .ENABLE(EN9), .CLK(CLK), .RST(RST), .DOUT(DOUT9));
  PC_Register_32_Bit R10 (.DIN(Write_Data), .ENABLE(EN10), .CLK(CLK), .RST(RST), .DOUT(DOUT10));
  PC_Register_32_Bit R11 (.DIN(Write_Data), .ENABLE(EN11), .CLK(CLK), .RST(RST), .DOUT(DOUT11));
  PC_Register_32_Bit R12 (.DIN(Write_Data), .ENABLE(EN12), .CLK(CLK), .RST(RST), .DOUT(DOUT12));
  PC_Register_32_Bit R13 (.DIN(Write_Data), .ENABLE(EN13), .CLK(CLK), .RST(RST), .DOUT(DOUT13));
  PC_Register_32_Bit R14 (.DIN(Write_Data), .ENABLE(EN14), .CLK(CLK), .RST(RST), .DOUT(DOUT14));
  PC_Register_32_Bit R15 (.DIN(Write_Data), .ENABLE(EN15), .CLK(CLK), .RST(RST), .DOUT(DOUT15));
  PC_Register_32_Bit R16 (.DIN(Write_Data), .ENABLE(Reg_Write), .CLK(CLK), .RST(RST), .DOUT(DOUT16));
  PC_Register_32_Bit R17 (.DIN(Write_Data), .ENABLE(EN17), .CLK(CLK), .RST(RST), .DOUT(DOUT17));
  PC_Register_32_Bit R18 (.DIN(Write_Data), .ENABLE(EN18), .CLK(CLK), .RST(RST), .DOUT(DOUT18));
  PC_Register_32_Bit R19 (.DIN(Write_Data), .ENABLE(EN19), .CLK(CLK), .RST(RST), .DOUT(DOUT19));
  PC_Register_32_Bit R20 (.DIN(Write_Data), .ENABLE(EN20), .CLK(CLK), .RST(RST), .DOUT(DOUT20));
  PC_Register_32_Bit R21 (.DIN(Write_Data), .ENABLE(EN21), .CLK(CLK), .RST(RST), .DOUT(DOUT21));
  PC_Register_32_Bit R22 (.DIN(Write_Data), .ENABLE(EN22), .CLK(CLK), .RST(RST), .DOUT(DOUT22));
  PC_Register_32_Bit R23 (.DIN(Write_Data), .ENABLE(EN23), .CLK(CLK), .RST(RST), .DOUT(DOUT23));
  PC_Register_32_Bit R24 (.DIN(Write_Data), .ENABLE(EN24), .CLK(CLK), .RST(RST), .DOUT(DOUT24));
  PC_Register_32_Bit R25 (.DIN(Write_Data), .ENABLE(EN25), .CLK(CLK), .RST(RST), .DOUT(DOUT25));
  PC_Register_32_Bit R26 (.DIN(Write_Data), .ENABLE(EN26), .CLK(CLK), .RST(RST), .DOUT(DOUT26));
  PC_Register_32_Bit R27 (.DIN(Write_Data), .ENABLE(EN27), .CLK(CLK), .RST(RST), .DOUT(DOUT27));
  PC_Register_32_Bit R28 (.DIN(Write_Data), .ENABLE(EN28), .CLK(CLK), .RST(RST), .DOUT(DOUT28));
  PC_Register_32_Bit R29 (.DIN(Write_Data), .ENABLE(EN29), .CLK(CLK), .RST(RST), .DOUT(DOUT29));
  PC_Register_32_Bit R30 (.DIN(Write_Data), .ENABLE(EN30), .CLK(CLK), .RST(RST), .DOUT(DOUT30));
  PC_Register_32_Bit R31 (.DIN(Write_Data), .ENABLE(EN31), .CLK(CLK), .RST(RST), .DOUT(DOUT31));
  Multiplexer #(.select(5), .width(32)) multiplexer_2 (
    .in0(DOUT0), .in1(DOUT1), .in2(DOUT2), .in3(DOUT3), .in4(DOUT4), .in5(DOUT5), .in6(DOUT6), .in7(DOUT7),
    .in8(DOUT8), .in9(DOUT9), .in10(DOUT10), .in11(DOUT11), .in12(DOUT12), .in13(DOUT13), .in14(DOUT14),
    .in15(DOUT15), .in16(DOUT16), .in17(DOUT17), .in18(DOUT18), .in19(DOUT19), .in20(DOUT20), .in21(DOUT21),
    .in22(DOUT22), .in23(DOUT23), .in24(DOUT24), .in25(DOUT25), .in26(DOUT26), .in27(DOUT27), .in28(DOUT28),
    .in29(DOUT29), .in30(DOUT30), .in31(DOUT31), .out(Read_Data2), .sel(MUX2));
  Decoder #(.select(5)) decoder_1 (
    .out0(EN0), .out1(EN1), .out2(EN2), .out3(EN3), .out4(EN4), .out5(EN5), .out6(EN6), .out7(EN7),
    .out8(EN8), .out9(EN9), .out10(EN10), .out11(EN11), .out12(EN12), .out13(EN13), .out14(EN14),
    .out15(EN15), .out16(EN16), .out17(EN17), .out18(EN18), .out19(EN19), .out20(EN20), .out21(EN21),
    .out22(EN22), .out23(EN23), .out24(EN24), .out25(EN25), .out26(EN26), .out27(EN27), .out28(EN28),
    .out29(EN29), .out30(EN30), .out31(EN31), .sel(Select_DEC1), .en(Reg_Write));

  // Other names for the same wires on the sheet: C = CLK; DIN[31:0] = Write_Data; EN = Reg_Write; R = RST

  // Notes on the sheet:
  //   Olayinka Olowookere
  //   ECE 422L
  //   Lab 9: Register File
endmodule
