// Logisim project ece422L_sign_extend.circ as structural Verilog
module Sign_Extend (
  input  [15:0] IN_16_BIT,
  output OUT_32_BIT
);

  wire [15:0] undriven;

  Multiplexer #(.width(16)) multiplexer_1 (.in0({16{1'b0}}), .in1(undriven), .sel(IN_16_BIT[15]));  // open: out
endmodule
