// Logisim project ece422L_microprocessor_design.circ as structural Verilog
module MIPS_Microprocessor (
  input  clk
);

  wire and_1_out, control_unit_1_alusrc, control_unit_1_branch, control_unit_1_memread,
       control_unit_1_memwrite, control_unit_1_regwrite, equality_check_alu_1_z;
  wire [1:0] control_unit_1_aluop1, sign_extend_1_out_32_bit_2;
  wire [3:0] adder_1_out, alu_control_unit_1_alucontrol;
  wire [4:0] multiplexer_1_out;
  wire [5:0] INSTRUCTION_MEMORY_p3;
  wire [25:0] INSTRUCTION_MEMORY_p6;
  wire [27:0] adder_1_out_2;
  wire [31:0] adder_2_out, DATA_MEMORY_dout, equality_check_alu_1_r_out, multiplexer_2_out,
       multiplexer_3_out, multiplexer_4_out, multiplexer_5_out, program_counter_1_dout, undriven, undriven_2;
  wire [31:2] sign_extend_1_out_32_bit;

  Program_Counter program_counter_1 (.DIN(multiplexer_2_out), .CLK(clk), .DOUT(program_counter_1_dout));
  // ROM #(.line("quad"), .misaligned("true")) INSTRUCTION_MEMORY: pin names not known; wires that end beside it: program_counter_1_dout, program_counter_1_dout[7:0], {INSTRUCTION_MEMORY_p3, INSTRUCTION_MEMORY_p6[25:24]}, INSTRUCTION_MEMORY_p6[23:16], INSTRUCTION_MEMORY_p6[15:8], INSTRUCTION_MEMORY_p6[7:0]
  Adder #(.width(32)) adder_1 (
    .a(program_counter_1_dout), .b(32'h4), .out({adder_1_out, adder_1_out_2}));  // open: cin, cout
  Multiplexer #(.width(5)) multiplexer_1 (
    .in0(INSTRUCTION_MEMORY_p6[25:21]), .in1(INSTRUCTION_MEMORY_p6[15:11]), .out(multiplexer_1_out));  // open: sel
  Adder #(.width(32)) adder_2 (
    .a({adder_1_out, adder_1_out_2}), .b({sign_extend_1_out_32_bit, 2'b00}), .out(adder_2_out));  // open: cin, cout
  Control_Unit control_unit_1 (
    .OPCODE(INSTRUCTION_MEMORY_p3), .ALUSrc(control_unit_1_alusrc), .RegWrite(control_unit_1_regwrite),
    .MemRead(control_unit_1_memread), .MemWrite(control_unit_1_memwrite), .Branch(control_unit_1_branch),
    .ALUOp1(control_unit_1_aluop1[0]), .ALUOp0(control_unit_1_aluop1[1]));  // open: RegDst, MemtoReg, Jump
  Sign_Extend sign_extend_1 (
    .IN_16_BIT(INSTRUCTION_MEMORY_p6[15:0]),
    .OUT_32_BIT({sign_extend_1_out_32_bit_2, sign_extend_1_out_32_bit}));
  ALU_Control_Unit alu_control_unit_1 (
    .ALUOp(control_unit_1_aluop1), .Funct(INSTRUCTION_MEMORY_p6[5:0]),
    .ALUControl(alu_control_unit_1_alucontrol));
  Multiplexer #(.width(32)) multiplexer_2 (
    .in0({adder_1_out, INSTRUCTION_MEMORY_p6, 2'b00}), .in1(multiplexer_3_out), .out(multiplexer_2_out));  // open: sel
  Multiplexer #(.width(32)) multiplexer_3 (
    .in0({adder_1_out, adder_1_out_2}), .in1(adder_2_out), .out(multiplexer_3_out), .sel(and_1_out));
  Multiplexer #(.width(32)) multiplexer_4 (
    .in0(undriven_2), .in1({sign_extend_1_out_32_bit_2, sign_extend_1_out_32_bit}), .out(multiplexer_4_out),
    .sel(control_unit_1_alusrc));
  and and_1 (and_1_out, equality_check_alu_1_z, control_unit_1_branch);
  Equality_Check_ALU equality_check_alu_1 (
    .ALU_CONTROL(alu_control_unit_1_alucontrol), .A(undriven), .B(multiplexer_4_out),
    .Z(equality_check_alu_1_z), .R_OUT(equality_check_alu_1_r_out));  // open: in_4, Overflow, C
  RAM #(.addrWidth(6), .dataWidth(32)) DATA_MEMORY (
    .addr(equality_check_alu_1_r_out[5:0]), .we(control_unit_1_memwrite), .oe(control_unit_1_memread),
    .clk(clk), .dout(DATA_MEMORY_dout));  // open: din
  Multiplexer #(.width(32)) multiplexer_5 (
    .in0(equality_check_alu_1_r_out), .in1(DATA_MEMORY_dout), .out(multiplexer_5_out));  // open: sel

  // Notes on the sheet:
  //   contents of INSTRUCTION_MEMORY (hex, n*v repeats v):
  //   6*0 8 8c 1 0 9 8c 3 0 9 11 20 40 8 1 0 0 8 ac 0 0 0 8 20 50 9 1 2 0 a ac
endmodule
