// Logisim project ece422L_sign_extend.circ as structural Verilog: 1 circuit, main circuit Sign_Extend
module Sign_Extend (
  input  [15:0] IN_16_BIT,
  output [31:0] OUT_32_BIT
);

  Multiplexer #(.width(16)) multiplexer_1 (
    .in0({16{1'b0}}), .in1({16{1'b1}}), .out(OUT_32_BIT[31:16]), .sel(IN_16_BIT[15]));

  assign OUT_32_BIT[15:0] = IN_16_BIT;
endmodule
