// Logisim project Lab_10.circ as structural Verilog: 3 circuits, main circuit Program_Counter
module Program_Counter (
  input  [31:0] DIN,
  input  CLK,
  output [31:0] DOUT
);

  PC_Register_32_Bit pc_register_32_bit_1 (.DIN(DIN), .ENABLE(1'b1), .CLK(CLK), .RST(1'b0), .DOUT(DOUT));

  // Notes on the sheet:
  //   Olayinka Olowookere
  //   ECE 422L
  //   Lab 10: Program Counter
endmodule

module Control_Unit (
  input  [5:0] OPCODE,
  output RegDst,
  output ALUSrc,
  output MemtoReg,
  output RegWrite,
  output MemRead,
  output MemWrite,
  output Branch,
  output ALUOp1,
  output ALUOp0,
  output Jump
);

  and and_1 (ALUOp1, ~OPCODE[5], ~OPCODE[4], ~OPCODE[3], ~OPCODE[2], ~OPCODE[1], ~OPCODE[0]);  // AND_Gate
  and and_2 (MemRead, OPCODE[5], ~OPCODE[4], ~OPCODE[3], ~OPCODE[2], OPCODE[1], OPCODE[0]);  // AND_Gate
  and and_3 (MemWrite, OPCODE[5], ~OPCODE[4], OPCODE[3], ~OPCODE[2], OPCODE[1], OPCODE[0]);  // AND_Gate
  and and_4 (ALUOp0, ~OPCODE[5], ~OPCODE[4], ~OPCODE[3], OPCODE[2], ~OPCODE[1], ~OPCODE[0]);  // AND_Gate
  and and_5 (Jump, ~OPCODE[5], ~OPCODE[4], ~OPCODE[3], ~OPCODE[2], OPCODE[1], ~OPCODE[0]);  // AND_Gate
  or or_1 (ALUSrc, MemRead, MemWrite);
  or or_2 (RegWrite, ALUOp1, MemRead);

  assign Branch = ALUOp0;
  assign MemtoReg = MemRead;
  assign RegDst = ALUOp1;
endmodule

module ALU_Control_Unit (
  input  [1:0] ALUOp,
  input  [5:0] Funct,
  output [3:0] ALUControl
);

  wire and_1_out, or_1_out;

  and and_1 (and_1_out, ALUOp[1], Funct[1]);
  or or_1 (or_1_out, Funct[3], Funct[0]);
  and and_2 (ALUControl[3], ALUOp[0], ~ALUOp[0]);  // AND_Gate
  or or_2 (ALUControl[2], ALUOp[0], and_1_out);
  or or_3 (ALUControl[1], ALUOp[1], Funct[2]);
  and and_3 (ALUControl[0], ALUOp[1], or_1_out);

  // Other names for the same wires on the sheet: ALU_Ctrl0 = ALUControl[0]; AluC[3:0] = ALUControl;
  //   ALU_Ctrl1 = ALUControl[1]; ALU_Ctrl2 = ALUControl[2]; ALU_Ctrl3 = ALUControl[3]; A0 = ALUOp[0]; A1 = ALUOp[1];
  //   F[5:0] = Funct; F0 = Funct[0]; F1 = Funct[1]; F2 = Funct[2]; F3 = Funct[3]
endmodule
