// Logisim project ece422L_register_32_bit_copy.circ as structural Verilog: 2 circuits, main circuit PC_Register_4_Bit
module PC_Register_4_Bit (
  input  [3:0] DIN,
  input  ENABLE,
  input  CLK,
  input  RST,
  output [3:0] DOUT
);

  wire multiplexer_1_out, multiplexer_2_out, multiplexer_3_out, multiplexer_4_out;

  D_Flip_Flop d_ff_1 (.D(multiplexer_1_out), .clk(CLK), .Q(DOUT[3]), .reset(RST));  // open: Qn, preset
  Multiplexer multiplexer_1 (.in0(DOUT[3]), .in1(DIN[3]), .out(multiplexer_1_out), .sel(ENABLE));
  D_Flip_Flop d_ff_2 (.D(multiplexer_2_out), .clk(CLK), .Q(DOUT[2]), .reset(RST));  // open: Qn, preset
  Multiplexer multiplexer_2 (.in0(DOUT[2]), .in1(DIN[2]), .out(multiplexer_2_out), .sel(ENABLE));
  D_Flip_Flop d_ff_3 (.D(multiplexer_3_out), .clk(CLK), .Q(DOUT[1]), .reset(RST));  // open: Qn, preset
  Multiplexer multiplexer_3 (.in0(DOUT[1]), .in1(DIN[1]), .out(multiplexer_3_out), .sel(ENABLE));
  D_Flip_Flop d_ff_4 (.D(multiplexer_4_out), .clk(CLK), .Q(DOUT[0]), .reset(RST));  // open: Qn, preset
  Multiplexer multiplexer_4 (.in0(DOUT[0]), .in1(DIN[0]), .out(multiplexer_4_out), .sel(ENABLE));

  // Other names for the same wires on the sheet: C = CLK; D0 = DIN[0]; D1 = DIN[1]; D2 = DIN[2]; D3 = DIN[3];
  //   Q0 = DOUT[0]; Q1 = DOUT[1]; Q2 = DOUT[2]; Q3 = DOUT[3]; EN = ENABLE; R = RST

  // Notes on the sheet:
  //   Olayinka Olowookere
  //   ECE 422L
  //   Lab 9: Register File
endmodule

module PC_Register_32_Bit (
  input  [31:0] DIN,
  input  ENABLE,
  input  CLK,
  input  RST,
  output [31:0] DOUT
);

  PC_Register_4_Bit pc_register_4_bit_1 (.DIN(DIN[3:0]), .ENABLE(ENABLE), .CLK(CLK), .RST(RST), .DOUT(DOUT[3:0]));
  PC_Register_4_Bit pc_register_4_bit_2 (.DIN(DIN[7:4]), .ENABLE(ENABLE), .CLK(CLK), .RST(RST), .DOUT(DOUT[7:4]));
  PC_Register_4_Bit pc_register_4_bit_3 (.DIN(DIN[11:8]), .ENABLE(ENABLE), .CLK(CLK), .RST(RST), .DOUT(DOUT[11:8]));
  PC_Register_4_Bit pc_register_4_bit_4 (.DIN(DIN[15:12]), .ENABLE(ENABLE), .CLK(CLK), .RST(RST), .DOUT(DOUT[15:12]));
  PC_Register_4_Bit pc_register_4_bit_5 (.DIN(DIN[19:16]), .ENABLE(ENABLE), .CLK(CLK), .RST(RST), .DOUT(DOUT[19:16]));
  PC_Register_4_Bit pc_register_4_bit_6 (.DIN(DIN[23:20]), .ENABLE(ENABLE), .CLK(CLK), .RST(RST), .DOUT(DOUT[23:20]));
  PC_Register_4_Bit pc_register_4_bit_7 (.DIN(DIN[27:24]), .ENABLE(ENABLE), .CLK(CLK), .RST(RST), .DOUT(DOUT[27:24]));
  PC_Register_4_Bit pc_register_4_bit_8 (.DIN(DIN[31:28]), .ENABLE(ENABLE), .CLK(CLK), .RST(RST), .DOUT(DOUT[31:28]));

  // Other names for the same wires on the sheet: C = CLK; D3_D0[3:0] = DIN[3:0]; D7_D4[3:0] = DIN[7:4];
  //   D11_D8[3:0] = DIN[11:8]; D15_D12[3:0] = DIN[15:12]; D19_D16[3:0] = DIN[19:16]; D23_D20[3:0] = DIN[23:20];
  //   D27_D24[3:0] = DIN[27:24]; D31_D28[3:0] = DIN[31:28]; Q3_Q0[3:0] = DOUT[3:0]; Q7_Q4[3:0] = DOUT[7:4];
  //   Q11_Q8[3:0] = DOUT[11:8]; Q15_Q12[3:0] = DOUT[15:12]; Q19_Q16[3:0] = DOUT[19:16]; Q23_Q20[3:0] = DOUT[23:20];
  //   Q27_Q24[3:0] = DOUT[27:24]; Q31_Q28[3:0] = DOUT[31:28]; EN = ENABLE; R = RST

  // Notes on the sheet:
  //   Olayinka Olowookere
  //   ECE 422L
  //   Lab 9: Register File
endmodule
